// Digital circuit cpu.dig as structural Verilog
module cpu (
  input  clk,
  input  [15:0] Test,
  input  RaIn,
  input  IRIn,
  input  ALUOut,
  input  [15:0] Test_2,
  input  Enable,
  input  RbIn,
  input  AROut,
  input  ARIn,
  input  MW,
  input  MR,
  input  Reset,
  input  PCIn,
  input  PCOut,
  input  PCInc,
  output [1:0] out_5,
  output Carry,
  output [15:0] Databus,
  output [15:0] Addressbus,
  output [15:0] out_17
);

  wire pulldown_1_out, pullup_1_out, pullup_2_out, RegIn;
  wire [1:0] counter_1_out;
  wire [2:0] Ra, Rb, RSel;
  wire [7:0] Decoder;
  wire [15:0] add_1_s, AR_q, Mem_q, PC_out, registerfile_1_da, registerfile_1_db;

  PullUp pullup_1 (.out(pullup_1_out));
  Counter #(.Bits(2)) counter_1 (.en(pullup_1_out), .C(clk), .clr(Reset), .out(counter_1_out));  // open: ovf
  PullUp pullup_2 (.out(pullup_2_out));
  ROM #(.AddrBits(10), .Bits(16)) Microcode (.A({Decoder, counter_1_out}), .sel(pullup_2_out), .D(out_17));
  PullDown pulldown_1 (.out(pulldown_1_out));
  Register #(.Bits(16)) AR (.D(Databus), .C(clk), .en(ARIn), .Q(AR_q));
  Register #(.Bits(16)) IR (.D(Test), .C(clk), .en(IRIn), .Q({out_5, Rb, Ra, Decoder}));
  CounterPreset #(.Bits(16), .isProgramCounter("true")) PC (
    .en(PCInc), .C(clk), .dir(pulldown_1_out), .in(Databus), .ld(PCIn), .clr(Reset), .out(PC_out));  // open: ovf
  Multiplexer #(.Bits(3)) multiplexer_1 (.sel(RbIn), .in_0(Ra), .in_1(Rb), .out(RSel));
  or or_1 (RegIn, RaIn, RbIn);
  assign Addressbus = PCOut ? PC_out : 16'bz;  // Driver driver_1
  assign Databus = Enable ? Test_2 : 16'bz;  // Driver driver_2
  assign Addressbus = AROut ? AR_q : 16'bz;  // Driver driver_3
  PullDown #(.Bits(16)) pulldown_2 (.out(Addressbus));
  PullDown #(.Bits(16)) pulldown_3 (.out(Databus));
  assign Databus = MR ? Mem_q : 16'bz;  // Driver driver_4
  RegisterFile #(.AddrBits(3), .Bits(16)) registerfile_1 (
    .Din(Databus), .we(RegIn), .Rw(RSel), .C(clk), .Ra(Ra), .Rb(Rb), .Da(registerfile_1_da),
    .Db(registerfile_1_db));
  RAMAsync #(.AddrBits(16), .isProgramMemory("true"), .Bits(16)) Mem (.A(Addressbus), .D(Databus), .we(MW), .Q(Mem_q));
  assign Databus = ALUOut ? add_1_s : 16'bz;  // Driver driver_5
  Add #(.Bits(16)) add_1 (.a(registerfile_1_da), .b(registerfile_1_db), .c_i(clk), .s(add_1_s), .c_o(Carry));

  // Notes on the sheet:
  //   Test: default 2560
  //   Test_2: default 1
  //   contents of Microcode (hex, n*v repeats v):
  //   1,2,3,4
endmodule
